// Logisim project Lab1Ex1.circ as structural Verilog: 1 circuit, main circuit main
module main (
  input  X,
  input  Y,
  output Z
);

  and and_1 (Z, X, Y);

  // Notes on the sheet:
  //   Basic 2-input AND Gate
endmodule
