// Logisim project Lab1Ex2.circ as structural Verilog: 1 circuit, main circuit main
module main (
  input  x1,
  input  x2,
  input  x3,
  input  y1,
  input  y2,
  input  y3,
  input  x5,
  input  x4,
  input  x6,
  input  y5,
  input  y4,
  input  y6,
  output z1,
  output z2,
  output z3,
  output z5,
  output z4,
  output z6
);

  and and_1 (z1, x1, y1);
  nand nand_1 (z4, x4, y4);
  or or_1 (z2, x2, y2);
  nor nor_1 (z5, x5, y5);
  xor xor_1 (z3, x3, y3);
  xnor xnor_1 (z6, x6, y6);

  // Notes on the sheet:
  //   Basic 2-input AND Gate
  //   Basic 2-input NAND Gate
  //   Basic 2-input OR Gate
  //   Basic 2-input NOR Gate
  //   Basic 2-input XOR Gate
  //   Basic 2-input XNOR Gate
endmodule
