// Logisim project Lab1Ex3.circ as structural Verilog: 1 circuit, main circuit main
module main (
  input  x1,
  input  y1,
  input  x2,
  input  y2,
  input  x3,
  input  y3,
  output z1,
  output z2,
  output z3
);

  and and_1 (z1, x1, y1);
  or or_1 (z2, x2, y2);
  xor xor_1 (z3, x3, y3);
endmodule
