// Logisim project Lab2Ex1.circ as structural Verilog: 1 circuit, main circuit main
module main (
  input  X,
  input  Y,
  output Sum,
  output Carry
);

  xor XOR (Sum, X, Y);
  and AND (Carry, Y, X);

  // Notes on the sheet:
  //   1-bit half adder
endmodule
