// Logisim project Lab2Ex3.circ as structural Verilog: 1 circuit, main circuit main
module main (
  input  a,
  input  b,
  input  c_in,
  output out_4,
  output out_5
);

  wire AND_2_out, AND_out, XOR_out;

  xor XOR (XOR_out, a, b);
  and AND (AND_out, b, a);
  and AND_2 (AND_2_out, c_in, XOR_out);
  xor XOR_2 (out_4, XOR_out, c_in);
  or OR (out_5, AND_2_out, AND_out);

  // Notes on the sheet:
  //   1-bit half adder
endmodule
