// Logisim project Lab2Ex4.circ as structural Verilog: 2 circuits, main circuit 1b_full_adder
module _1b_full_adder (
  input  in_1,
  input  in_2,
  input  in_3,
  output out_4,
  output out_5
);

  wire AND_2_out, AND_out, XOR_out;

  xor XOR (XOR_out, in_1, in_2);
  buf AND (AND_out, in_1);  // AND_Gate
  and AND_2 (AND_2_out, in_3, XOR_out);
  xor XOR_2 (out_4, XOR_out, in_3);
  or OR (out_5, AND_2_out, AND_out);
endmodule

module main (
  input  [7:0] A,
  input  [7:0] B,
  output [7:0] Sum,
  output Carry_Out
);

  wire n1b_full_adder_1_out_5, n1b_full_adder_3_out_5, n1b_full_adder_4_out_5, n1b_full_adder_5_out_5,
       n1b_full_adder_6_out_5, n1b_full_adder_7_out_5;
  wire [7:0] not_1_out;

  assign not_1_out = ~B;  // NOT_Gate not_1, 8 bits wide
  _1b_full_adder u_1b_full_adder_1 (
    .in_1(A[0]), .in_2(not_1_out[0]), .in_3(1'b1), .out_4(Sum[0]), .out_5(n1b_full_adder_1_out_5));
  _1b_full_adder u_1b_full_adder_2 (
    .in_1(A[1]), .in_2(not_1_out[1]), .in_3(n1b_full_adder_1_out_5), .out_4(Sum[1]), .out_5(not_1_out[2]));
  _1b_full_adder u_1b_full_adder_3 (
    .in_1(A[2]), .in_2(not_1_out[2]), .in_3(not_1_out[2]), .out_4(Sum[2]), .out_5(n1b_full_adder_3_out_5));
  _1b_full_adder u_1b_full_adder_4 (
    .in_1(A[3]), .in_2(not_1_out[3]), .in_3(n1b_full_adder_3_out_5), .out_4(Sum[3]),
    .out_5(n1b_full_adder_4_out_5));
  _1b_full_adder u_1b_full_adder_5 (
    .in_1(A[4]), .in_2(not_1_out[4]), .in_3(n1b_full_adder_4_out_5), .out_4(Sum[4]),
    .out_5(n1b_full_adder_5_out_5));
  _1b_full_adder u_1b_full_adder_6 (
    .in_1(A[5]), .in_2(not_1_out[5]), .in_3(n1b_full_adder_5_out_5), .out_4(Sum[5]),
    .out_5(n1b_full_adder_6_out_5));
  _1b_full_adder u_1b_full_adder_7 (
    .in_1(A[6]), .in_2(not_1_out[6]), .in_3(n1b_full_adder_6_out_5), .out_4(Sum[6]),
    .out_5(n1b_full_adder_7_out_5));
  _1b_full_adder u_1b_full_adder_8 (
    .in_1(A[7]), .in_2(not_1_out[7]), .in_3(n1b_full_adder_7_out_5), .out_4(Sum[7]), .out_5(Carry_Out));
endmodule
