// Logisim project Lab5_Ex1.circ as structural Verilog: 11 circuits, main circuit main
module main (
  input  [3:0] A,
  input  [3:0] B,
  input  C_In,
  input  [2:0] S,
  output [3:0] out_5,
  output [3:0] out_6,
  output C_in_2,
  output V
);

  wire A_1_carry_out, A_B_2_c_out, A_B_2_v, A_B_c_out, A_B_v, B_A_c_out, B_A_v, n7_segment_1_a,
       n7_segment_1_b, n7_segment_1_c, n7_segment_1_d, n7_segment_1_e, n7_segment_1_f, n7_segment_1_g,
       not_1_out, not_2_out, not_3_out;
  wire [3:0] A_1_sum, A_B_2_out_4, A_B_out_4, and_1_out, B_A_out_4, or_1_out, xnor_1_out, xor_1_out;

  _1 A_1 (.A(A), .in_2(C_In), .Sum(A_1_sum), .Carry_Out(A_1_carry_out));
  overflow A_B (.A(A), .B(B), .C_in(C_In), .out_4(A_B_out_4), .V(A_B_v), .C_out(A_B_c_out));
  overflow A_B_2 (.A(A), .B(B), .C_in(not_1_out), .out_4(A_B_2_out_4), .V(A_B_2_v), .C_out(A_B_2_c_out));
  not not_1 (not_1_out, C_In);
  overflow B_A (.A(B), .B(A), .C_in(not_2_out), .out_4(B_A_out_4), .V(B_A_v), .C_out(B_A_c_out));
  not not_2 (not_2_out, C_In);
  assign and_1_out = A & B;  // AND_Gate and_1, 4 bits wide
  assign or_1_out = A | B;  // OR_Gate or_1, 4 bits wide
  assign xor_1_out = A ^ B;  // XOR_Gate xor_1, 4 bits wide
  assign xnor_1_out = ~(A ^ B);  // XNOR_Gate xnor_1, 4 bits wide
  not not_3 (not_3_out, S[2]);
  Multiplexer #(.select(2)) multiplexer_1 (
    .in0(A_1_carry_out), .in1(A_B_c_out), .in2(A_B_2_c_out), .in3(B_A_c_out), .out(C_in_2), .sel(S[1:0]),
    .en(S[2]));
  Multiplexer #(.select(2)) multiplexer_2 (
    .in0(1'b0), .in1(A_B_v), .in2(A_B_2_v), .in3(B_A_v), .out(V), .sel(S[1:0]), .en(S[2]));
  Multiplexer #(.select(2), .width(4)) multiplexer_3 (
    .in0(and_1_out), .in1(or_1_out), .in2(xor_1_out), .in3(xnor_1_out), .out(out_5), .sel(S[1:0]),
    .en(not_3_out));
  Multiplexer #(.select(2), .width(4)) multiplexer_4 (
    .in0(A_1_sum), .in1(A_B_out_4), .in2(A_B_2_out_4), .in3(B_A_out_4), .out(out_6), .sel(S[1:0]), .en(S[2]));
  LED led_1 (.in(out_5[0]));
  LED led_2 (.in(out_5[1]));
  LED led_3 (.in(out_5[2]));
  LED led_4 (.in(out_5[3]));
  _7_segment u_7_segment_1 (
    .D3(out_6[3]), .D2(out_6[2]), .D1(out_6[1]), .D0(out_6[0]), .a(n7_segment_1_a), .b(n7_segment_1_b),
    .c(n7_segment_1_c), .d(n7_segment_1_d), .e(n7_segment_1_e), .f(n7_segment_1_f), .g(n7_segment_1_g));
  _7_Segment_Display u_7_segment_display_1 (
    .g(n7_segment_1_g), .f(n7_segment_1_f), .a(n7_segment_1_a), .b(n7_segment_1_b), .e(n7_segment_1_e),
    .d(n7_segment_1_d), .c(n7_segment_1_c));  // open: dp
endmodule

module adder (
  input  a,
  input  b,
  input  c_in,
  output Sum,
  output c_out
);

  wire AND_2_out, AND_out, XOR_out;

  xor XOR (XOR_out, a, b);
  and AND (AND_out, b, a);
  and AND_2 (AND_2_out, c_in, XOR_out);
  xor XOR_2 (Sum, XOR_out, c_in);
  or OR (c_out, AND_2_out, AND_out);

  // Notes on the sheet:
  //   1-bit full adder
endmodule

module _2 (
  input  [3:0] A,
  input  [3:0] B,
  output [3:0] Sum,
  output Carry_Out
);

  wire adder_1_c_out, adder_2_c_out, adder_3_c_out;

  // Probe on A
  // Probe on B
  adder adder_1 (.a(A[0]), .b(B[0]), .c_in(1'b0), .Sum(Sum[0]), .c_out(adder_1_c_out));
  adder adder_2 (.a(A[1]), .b(B[1]), .c_in(adder_1_c_out), .Sum(Sum[1]), .c_out(adder_2_c_out));
  adder adder_3 (.a(A[2]), .b(B[2]), .c_in(adder_2_c_out), .Sum(Sum[2]), .c_out(adder_3_c_out));
  adder adder_4 (.a(A[3]), .b(B[3]), .c_in(adder_3_c_out), .Sum(Sum[3]), .c_out(Carry_Out));
  // Probe on Sum
endmodule

module _1 (
  input  [3:0] A,
  input  in_2,
  output [3:0] Sum,
  output Carry_Out
);

  wire adder_1_c_out, adder_2_c_out, adder_3_c_out;

  // Probe on A
  adder adder_1 (.a(A[0]), .b(1'b0), .c_in(in_2), .Sum(Sum[0]), .c_out(adder_1_c_out));
  adder adder_2 (.a(A[1]), .b(1'b0), .c_in(adder_1_c_out), .Sum(Sum[1]), .c_out(adder_2_c_out));
  adder adder_3 (.a(A[2]), .b(1'b0), .c_in(adder_2_c_out), .Sum(Sum[2]), .c_out(adder_3_c_out));
  adder adder_4 (.a(A[3]), .b(1'b0), .c_in(adder_3_c_out), .Sum(Sum[3]), .c_out(Carry_Out));
  // Probe on Sum
endmodule

module _3 (
  input  [3:0] A,
  input  [3:0] B,
  output [3:0] Sum,
  output Carry_Out
);

  wire subtractor_a_b_1_c_out, subtractor_a_b_2_c_out, subtractor_a_b_3_c_out;

  // Probe on A
  // Probe on B
  subtractor__A_B subtractor_a_b_1 (.a(A[0]), .b(B[0]), .c_in(1'b0), .Sum(Sum[0]), .c_out(subtractor_a_b_1_c_out));
  subtractor__A_B subtractor_a_b_2 (
    .a(A[1]), .b(B[1]), .c_in(subtractor_a_b_1_c_out), .Sum(Sum[1]), .c_out(subtractor_a_b_2_c_out));
  subtractor__A_B subtractor_a_b_3 (
    .a(A[2]), .b(B[2]), .c_in(subtractor_a_b_2_c_out), .Sum(Sum[2]), .c_out(subtractor_a_b_3_c_out));
  subtractor__A_B subtractor_a_b_4 (.a(A[3]), .b(B[3]), .c_in(subtractor_a_b_3_c_out), .Sum(Sum[3]), .c_out(Carry_Out));
  // Probe on Sum
endmodule

module _4 (
  input  [3:0] A,
  input  [3:0] B,
  output [3:0] Sum,
  output Carry_Out
);

  // Probe on A
  // Probe on B
  // Probe on Sum
endmodule

module subtractor__A_B (
  input  a,
  input  b,
  input  c_in,
  output Sum,
  output c_out
);

  wire AND_2_out, AND_out, not_1_out, not_2_out, XOR_out;

  xor XOR (XOR_out, a, b);
  not not_1 (not_1_out, b);
  not not_2 (not_2_out, XOR_out);
  and AND (AND_out, not_1_out, a);
  and AND_2 (AND_2_out, c_in, not_2_out);
  xor XOR_2 (Sum, XOR_out, c_in);
  or OR (c_out, AND_2_out, AND_out);
endmodule

module subtract__B_A (
  input  a,
  input  b,
  input  c_in,
  output Sum,
  output c_out
);

  wire AND_2_out, AND_out, not_1_out, not_2_out, XOR_out;

  xor XOR (XOR_out, a, b);
  not not_1 (not_1_out, a);
  and AND (AND_out, b, not_1_out);
  not not_2 (not_2_out, c_in);
  and AND_2 (AND_2_out, not_2_out, XOR_out);
  xor XOR_2 (Sum, XOR_out, c_in);
  or OR (c_out, AND_2_out, AND_out);
endmodule

module add_for_1 (
  input  a,
  input  c_in,
  output Sum,
  output c_out
);

  wire AND_2_out, AND_out, XOR_out;

  xor XOR (XOR_out, a, 1'b1);
  and AND (AND_out, 1'b1, a);
  and AND_2 (AND_2_out, c_in, XOR_out);
  xor XOR_2 (Sum, XOR_out, c_in);
  or OR (c_out, AND_2_out, AND_out);

  // Notes on the sheet:
  //   1-bit full adder
endmodule

module overflow (
  input  [3:0] A,
  input  [3:0] B,
  input  C_in,
  output [3:0] out_4,
  output V,
  output C_out
);

  wire adder_1_c_out, adder_2_c_out, adder_3_c_out, xor_1_out, xor_2_out, xor_3_out, xor_4_out;

  xor xor_1 (xor_1_out, B[0], C_in);
  xor xor_2 (xor_2_out, B[1], C_in);
  xor xor_3 (xor_3_out, B[2], C_in);
  xor xor_4 (xor_4_out, B[3], C_in);
  adder adder_1 (.a(A[0]), .b(xor_1_out), .c_in(C_in), .Sum(out_4[0]), .c_out(adder_1_c_out));
  adder adder_2 (.a(A[1]), .b(xor_2_out), .c_in(adder_1_c_out), .Sum(out_4[1]), .c_out(adder_2_c_out));
  adder adder_3 (.a(A[2]), .b(xor_3_out), .c_in(adder_2_c_out), .Sum(out_4[2]), .c_out(adder_3_c_out));
  adder adder_4 (.a(A[3]), .b(xor_4_out), .c_in(adder_3_c_out), .Sum(out_4[3]), .c_out(C_out));
  xor xor_5 (V, adder_3_c_out, C_out);
endmodule

module _7_segment (
  input  D3,
  input  D2,
  input  D1,
  input  D0,
  output a,
  output b,
  output c,
  output d,
  output e,
  output f,
  output g
);

  wire and_1_out, and_2_out, and_3_out, and_4_out, and_5_out, and_6_out, and_7_out, and_8_out, and_9_out,
       and_10_out, and_11_out, and_12_out, and_13_out, and_14_out, and_15_out, and_16_out, not_1_out,
       not_2_out, not_3_out, not_4_out, not_5_out, not_6_out, not_7_out, not_8_out, not_9_out, not_10_out,
       not_11_out, not_12_out, not_13_out, not_14_out, not_15_out, not_16_out, not_17_out, not_18_out,
       not_19_out, not_20_out, not_21_out;

  not not_1 (not_1_out, D2);
  and and_1 (and_1_out, not_1_out, not_2_out);
  not not_2 (not_2_out, D0);
  and and_2 (and_2_out, D2, D0);
  not not_3 (not_3_out, D2);
  not not_4 (not_4_out, D1);
  and and_3 (and_3_out, not_4_out, not_5_out);
  not not_5 (not_5_out, D0);
  and and_4 (and_4_out, D1, D0);
  not not_6 (not_6_out, D1);
  or or_1 (c, not_6_out, D0, D2);
  not not_7 (not_7_out, D2);
  and and_5 (and_5_out, not_7_out, not_8_out);
  not not_8 (not_8_out, D0);
  not not_9 (not_9_out, D2);
  and and_6 (and_6_out, not_9_out, D1);
  and and_7 (and_7_out, D1, not_10_out);
  not not_10 (not_10_out, D0);
  and and_8 (and_8_out, D2, not_11_out, D0);
  not not_11 (not_11_out, D1);
  not not_12 (not_12_out, D2);
  and and_9 (and_9_out, not_12_out, not_13_out);
  not not_13 (not_13_out, D0);
  and and_10 (and_10_out, D1, not_14_out);
  not not_14 (not_14_out, D0);
  not not_15 (not_15_out, D1);
  and and_11 (and_11_out, not_15_out, not_16_out);
  not not_16 (not_16_out, D0);
  and and_12 (and_12_out, D2, not_17_out);
  not not_17 (not_17_out, D1);
  and and_13 (and_13_out, D2, not_18_out);
  not not_18 (not_18_out, D0);
  not not_19 (not_19_out, D2);
  and and_14 (and_14_out, not_19_out, D1);
  and and_15 (and_15_out, D2, not_20_out);
  not not_20 (not_20_out, D1);
  and and_16 (and_16_out, D2, not_21_out);
  not not_21 (not_21_out, D0);
  or or_2 (a, and_1_out, D1, and_2_out, D3);
  or or_3 (b, not_3_out, and_3_out, and_4_out);
  or or_4 (d, and_5_out, and_6_out, and_7_out, and_8_out, D3);
  or or_5 (e, and_9_out, and_10_out);
  or or_6 (f, and_11_out, and_12_out, and_13_out, D3);
  or or_7 (g, and_14_out, and_15_out, and_16_out, D3);
  _7_Segment_Display u_7_segment_display_1 (.g(g), .f(f), .a(a), .b(b), .e(e), .d(d), .c(c));  // open: dp
endmodule
