// Logisim project Lab6_Ex2.circ as structural Verilog: 1 circuit, main circuit main
module main (
  input  X,
  output Y,
  output A,
  output B,
  output C
);

  wire and_1_out, and_2_out, and_3_out, and_4_out, and_5_out, and_6_out, clock_1_out, d_ff_1_qn, d_ff_2_qn,
       d_ff_3_qn, not_1_out, or_1_out, or_2_out;

  and and_1 (and_1_out, B, C, X);
  and and_2 (and_2_out, B, d_ff_3_qn);
  and and_3 (and_3_out, A, X);
  and and_4 (and_4_out, d_ff_2_qn, C, X);
  and and_5 (and_5_out, d_ff_1_qn, d_ff_2_qn, d_ff_3_qn, X);
  and and_6 (and_6_out, B, d_ff_3_qn, not_1_out);
  not not_1 (not_1_out, X);
  or or_1 (or_1_out, and_2_out, and_3_out, and_4_out);
  or or_2 (or_2_out, and_5_out, and_6_out);
  Clock clock_1 (.out(clock_1_out));
  D_Flip_Flop d_ff_1 (.clk(clock_1_out), .D(and_1_out), .Q(A), .Qn(d_ff_1_qn));  // open: preset, en, reset
  D_Flip_Flop d_ff_2 (.clk(clock_1_out), .D(or_1_out), .Q(B), .Qn(d_ff_2_qn));  // open: preset, en, reset
  D_Flip_Flop d_ff_3 (.clk(clock_1_out), .D(or_2_out), .Q(C), .Qn(d_ff_3_qn));  // open: preset, en, reset

  assign Y = A;

  // Notes on the sheet:
  //   B
  //   X
  //   A
  //   C
  //   X'
  //   B'
  //   A'
  //   C'
endmodule
