// Logisim project Lab6_Ex3.circ as structural Verilog: 1 circuit, main circuit main
module main (
  input  X,
  output Y,
  output A,
  output B
);

  wire and_1_out, and_2_out, and_3_out, clock_1_out, j_k_ff_1_qn, j_k_ff_2_qn, not_1_out, or_1_out, or_2_out;

  not not_1 (not_1_out, X);
  and and_1 (and_1_out, B, X);
  and and_2 (and_2_out, j_k_ff_1_qn, X);
  and and_3 (and_3_out, A, not_1_out);
  or or_1 (or_1_out, and_2_out, and_3_out);
  or or_2 (or_2_out, j_k_ff_1_qn, not_1_out);
  Clock clock_1 (.out(clock_1_out));
  J_K_Flip_Flop j_k_ff_1 (.J(and_1_out), .clk(clock_1_out), .K(B), .Q(A), .Qn(j_k_ff_1_qn));  // open: preset, en, reset
  J_K_Flip_Flop j_k_ff_2 (
    .J(or_1_out), .clk(clock_1_out), .K(or_2_out), .Q(B), .Qn(j_k_ff_2_qn));  // open: preset, en, reset
  and and_4 (Y, A, B, X);

  // Notes on the sheet:
  //   A'
  //   X'
  //   A
  //   X
  //   B'
  //   B
endmodule
